# Fritzing sketch VidBoi (saved by Fritzing 0.9.3b)
circuit board: 6.52541cm x 3.09829cm
breadboards: 1

parts:
  CV_In_1 = 3.5mm Audio Jack [package=audio-jack-3.5mm-smd]
  MCU1 = Raspberry Pi Zero
  IC1 = MCP3008 8-channel 10-bit ADC [part_number=MCP3008]
  CV_In_2 = 3.5mm Audio Jack [package=audio-jack-3.5mm-smd]
  CV_In_3 = 3.5mm Audio Jack [package=audio-jack-3.5mm-smd]
  Knob2 = Rotary Potentiometer (Small) [maximum_resistance=10kΩ package=THT]
  Btn_1 = SWITCH-MOMENTARY-2 [package=tactile-pth-12mm]
  Knob3 = Rotary Potentiometer (Small) [maximum_resistance=10kΩ package=THT]
  Knob1 = Rotary Potentiometer (Small) [maximum_resistance=10kΩ package=THT]
  PCB3 = Raspberry Pi Shield  # not connected
  R1 = Resistor [tolerance=±5% resistance=10k package="1206 [SMD]"]
  R4 = Resistor [tolerance=±5% resistance=10k package="1206 [SMD]"]
  R2 = Resistor [tolerance=±5% resistance=10k package="1206 [SMD]"]
  R3 = Resistor [tolerance=±5% resistance=10k package="1206 [SMD]"]
  IC2 = IC, DIP package, 16 pins [chip_label=MCP3008]  # not connected

nets (from the schematic view):
  N1: CV_In_1.RIGHT, R1.Pin_0
  GND: CV_In_1.LEFT, CV_In_2.LEFT, CV_In_3.LEFT, Knob2.leg1, Knob3.leg1, Knob1.leg1
  N2: MCU1.pin_1, MCU1.pin_17, IC1.no_name_yet#15, IC1.no_name_yet#16
  N3: MCU1.pin_18, IC1.no_name_yet#13
  N4: MCU1.pin_20, MCU1.pin_25, MCU1.pin_39, IC1.no_name_yet#9, IC1.no_name_yet#10, IC1.no_name_yet#14
  N5: MCU1.pin_23, IC1.no_name_yet#12
  N6: MCU1.pin_24, IC1.no_name_yet#11
  N7: MCU1.pin_37, R4.Pin_1
  N8: IC1.no_name_yet#1, R1.Pin_1
  N9: IC1.no_name_yet#2, R2.Pin_1
  N10: IC1.no_name_yet#3, R3.Pin_1
  N11: IC1.no_name_yet#4, Knob1.wiper
  N12: IC1.no_name_yet#5, Knob2.wiper
  N13: IC1.no_name_yet#6, Knob3.wiper
  N14: CV_In_2.RIGHT, R2.Pin_0
  N15: CV_In_3.RIGHT, R3.Pin_0
  5V: Knob2.leg2, Btn_1.1, Knob3.leg2, Knob1.leg2
  N16: Btn_1.2, R4.Pin_0

notes:
  CV Inputs
  Button
  Knobs

custom parts:
  Raspberry Pi Shield: Plain PCB Shaped to fit as Raspberry Pi "Shield"
